// Logisim project item_c.circ as structural Verilog: 1 circuit, main circuit main
module main (
  input  A,
  input  B,
  input  C,
  input  D,
  output X
);

  wire and_1_out, or_1_out;

  and and_1 (and_1_out, A, B);
  or or_1 (or_1_out, C, D);
  and and_2 (X, and_1_out, or_1_out);

  // Notes on the sheet:
  //   QUESTÃO 1
  //   c)
endmodule
